# Fritzing sketch Pong_Schematic (saved by Fritzing 0.9.3b)
breadboards: 1

parts:
  Part1 = Arduino Uno (Rev3)
  LCD1 = LCD screen
  R1 = Rotary Potentiometer (Small) [maximum_resistance=100kΩ package=THT]
  J1 = Piezo Speaker
  LED1 = RGB LED (com. cathode, rgb) [package="5 mm [THT]"]

nets:
  N1: Part1.A0, R1.wiper
  N2: Part1.D9_PWM, J1.pin1
  N3: Part1.D10_PWM/SS, LCD1.V0
  N4: Part1.D12/MISO, LCD1.RS
  N5: Part1.D13/SCK, LED1.red_anode
  N6: Part1.D2, LCD1.DB7
  N7: Part1.D3_PWM, LCD1.DB6
  N8: Part1.D4, LCD1.DB5
  N9: Part1.D5_PWM, LCD1.DB4
  N10: Part1.D6_PWM, LED1.blue_anode
  N11: Part1.D7, LED1.green_anode
  5V: Part1.5V, LCD1.VDD, LCD1.LED+, R1.leg1, R1.leg2
  GND: Part1.GND, LCD1.VSS, LCD1.R/W, LCD1.LED-, J1.pin2, LED1.common_cathode
